// Logisim project and.circ as structural Verilog: 1 circuit, main circuit main
module main (
  input  in_1,
  input  in_2,
  input  in_3,
  input  in_4,
  output out_5
);

  wire and_1_out, and_2_out;

  and and_1 (and_1_out, in_3, in_4);
  and and_2 (and_2_out, in_1, in_2);
  and and_3 (out_5, and_2_out, and_1_out);
endmodule
