// Logisim project full.circ as structural Verilog: 1 circuit, main circuit main
module main (
  input  in_1,
  input  in_2,
  input  in_3,
  input  in_4,
  input  in_5,
  output out_6
);

  wire and_1_out, and_2_out, not_1_out, or_1_out;

  not not_1 (not_1_out, in_1);
  and and_1 (and_1_out, in_2, in_3);
  or or_1 (or_1_out, in_4, in_5);
  and and_2 (and_2_out, and_1_out, or_1_out);
  and and_3 (out_6, and_2_out, not_1_out);
endmodule
